// Logisim project cpu.circ as structural Verilog: 1 circuit, main circuit main
module main (
  input  CLK_RUN,
  input  [7:0] in_2,
  input  [15:0] in_3,
  input  in_4,
  input  in_5,
  output [3:0] out_6,
  output [7:0] out_7,
  output [15:0] out_8,
  output [15:0] out_9,
  output [7:0] out_10,
  output [7:0] out_11,
  output [15:0] out_12,
  output [7:0] out_13,
  output [7:0] out_14,
  output [7:0] out_15,
  output [7:0] L_Register,
  output [7:0] out_17,
  output [15:0] out_18,
  output [7:0] _C_Z,
  output [7:0] out_20,
  output [15:0] out_21,
  output [7:0] out_22,
  output [15:0] out_23,
  output [7:0] out_24,
  output [7:0] out_25
);

  wire A_TO_DATA, A_TO_X, adder_1_cout, ADDR_HI_TO_DATA, ADDR_LO_TO_DATA, ADDR_TO_HL, ADDR_TO_IP,
       ADDR_TO_MAR, ADDR_TO_SP, ADDR_TO_T, and_1_out, and_2_out, and_4_out, and_5_out, and_6_out, and_7_out,
       and_8_out, and_9_out, and_10_out, and_11_out, B_TO_DATA, C_TO_DATA, CARRY, CLK, CLK_STEP_out,
       clock_1_out, d_ff_1_q, d_ff_2_q, D_TO_DATA, DATA_TO_A, DATA_TO_ADDR_HI, DATA_TO_ADDR_LO, DATA_TO_B,
       DATA_TO_C, DATA_TO_D, DATA_TO_IR, DATA_TO_MDR, DATA_TO_Y, FLAGS, H_TO_DATA, HL_TO_ADDR, HLT, HRST_out,
       IP_INC, IP_TO_ADDR, L_TO_DATA, MAR_INC, MDR_TO_DATA, minus_CLK, nor_1_out, not_1_out, not_2_out,
       not_3_out, not_5_out, NXT, or_2_out, or_3_out, or_4_out, or_5_out, or_6_out, or_7_out, or_8_out,
       or_9_out, or_10_out, or_11_out, or_12_out, RST, SP_DEC, SP_INC, SP_TO_ADDR, SRST, SUB, T_RST,
       T_TO_ADDR, xor_1_out, xor_3_out, Z_TO_DATA;
  wire [2:0] rom_2_data, rom_2_data_2, rom_3_data_2;
  wire [2:2] rom_3_data;
  wire [7:0] bit_extender_1_out, xor_2_out;
  wire [7:6] rom_2_data_3;

  Button CLK_STEP (.out(CLK_STEP_out));
  Button HRST (.out(HRST_out));
  Clock clock_1 (.out(clock_1_out));
  and and_1 (and_1_out, clock_1_out, CLK_RUN);
  not not_1 (not_1_out, CLK_RUN);
  and and_2 (and_2_out, not_1_out, CLK_STEP_out);
  or or_1 (RST, HRST_out, SRST);
  not not_2 (not_2_out, NXT);
  or or_2 (or_2_out, and_1_out, and_2_out);
  not not_3 (not_3_out, HLT);
  Demultiplexer #(.select(3)) demultiplexer_1 (
    .out1(DATA_TO_A), .out2(DATA_TO_B), .out3(DATA_TO_C), .out4(DATA_TO_D), .out5(DATA_TO_MDR),
    .out6(DATA_TO_ADDR_HI), .out7(DATA_TO_ADDR_LO), .in(1'b1), .sel(rom_2_data), .en(1'b1));  // open: out0
  Counter #(.width(4), .max('hf)) counter_1 (
    .load(NXT), .D(4'b0000), .count(not_2_out), .Q(out_6), .clk(minus_CLK), .clr(RST));  // open: carry
  not not_4 (minus_CLK, CLK);
  and and_3 (CLK, or_2_out, not_3_out);
  assign bit_extender_1_out = {{7{SUB}}, SUB};  // Bit_Extender bit_extender_1
  ROM #(.addrWidth(15)) rom_1 (
    .addr({1'b0, _C_Z[1:0], out_6, out_10}),
    .data({Z_TO_DATA, FLAGS, SUB, DATA_TO_Y, A_TO_X, NXT, SRST, HLT}), .sel(1'b1));
  Register register_1 (.D(out_7), .en(DATA_TO_IR), .Q(out_10), .clk(CLK), .clr(RST));
  Register register_2 (.D(out_7), .en(DATA_TO_A), .Q(out_11), .clk(CLK));  // open: clr
  Register register_3 (.D(out_11), .en(A_TO_X), .Q(out_13), .clk(CLK));  // open: clr
  xor xor_1 (xor_1_out, CARRY, SUB);
  assign xor_2_out = bit_extender_1_out ^ out_20;  // XOR_Gate xor_2, 8 bits wide
  Register register_4 (.D(out_7), .en(DATA_TO_Y), .Q(out_20), .clk(CLK));  // open: clr
  Register register_5 (.D(out_7), .en(DATA_TO_B), .Q(out_22), .clk(CLK));  // open: clr
  Register register_6 (.D(out_7), .en(DATA_TO_C), .Q(out_24), .clk(CLK));  // open: clr
  Register register_7 (.D(out_7), .en(DATA_TO_D), .Q(out_25), .clk(CLK));  // open: clr
  assign out_7 = A_TO_DATA ? out_11 : 8'bz;  // Controlled_Buffer controlled_buffer_1
  Adder adder_1 (.a(out_13), .b(xor_2_out), .out(out_14), .cin(xor_1_out), .cout(adder_1_cout));
  xor xor_3 (xor_3_out, adder_1_cout, SUB);
  assign out_7 = B_TO_DATA ? out_22 : 8'bz;  // Controlled_Buffer controlled_buffer_2
  assign out_7 = C_TO_DATA ? out_24 : 8'bz;  // Controlled_Buffer controlled_buffer_3
  assign out_7 = D_TO_DATA ? out_25 : 8'bz;  // Controlled_Buffer controlled_buffer_4
  Demultiplexer #(.select(3)) demultiplexer_2 (
    .out1(A_TO_DATA), .out2(B_TO_DATA), .out3(C_TO_DATA), .out4(D_TO_DATA), .out5(MDR_TO_DATA),
    .out6(ADDR_HI_TO_DATA), .out7(ADDR_LO_TO_DATA), .in(1'b1), .sel(rom_2_data_2), .en(1'b1));  // open: out0
  assign out_7 = Z_TO_DATA ? out_14 : 8'bz;  // Controlled_Buffer controlled_buffer_5
  nor nor_1 (nor_1_out, out_14[0], out_14[1], out_14[2], out_14[3], out_14[4], out_14[5], out_14[6], out_14[7]);
  D_Flip_Flop d_ff_1 (.clk(CLK), .D(nor_1_out), .Q(d_ff_1_q), .en(Z_TO_DATA));  // open: Qn, preset, reset
  D_Flip_Flop d_ff_2 (.clk(CLK), .D(xor_3_out), .Q(d_ff_2_q), .en(Z_TO_DATA));  // open: Qn, preset, reset
  ROM #(.addrWidth(15)) rom_2 (
    .addr({1'b0, _C_Z[1:0], out_6, out_10}), .data({rom_2_data_3, rom_2_data_2, rom_2_data}), .sel(1'b1));
  D_Flip_Flop d_ff_3 (.clk(CLK), .D(d_ff_1_q), .Q(_C_Z[0]), .en(FLAGS), .reset(RST));  // open: Qn, preset
  D_Flip_Flop d_ff_4 (.clk(CLK), .D(d_ff_2_q), .Q(_C_Z[1]), .en(FLAGS), .reset(RST));  // open: Qn, preset
  assign out_7 = in_4 ? in_2 : 8'bz;  // Controlled_Buffer controlled_buffer_6
  assign out_7 = MDR_TO_DATA ? out_15 : 8'bz;  // Controlled_Buffer controlled_buffer_7
  assign out_7 = L_TO_DATA ? L_Register : 8'bz;  // Controlled_Buffer controlled_buffer_8
  assign out_7 = H_TO_DATA ? out_17 : 8'bz;  // Controlled_Buffer controlled_buffer_9
  not not_5 (not_5_out, DATA_TO_MDR);
  assign out_15 = DATA_TO_MDR ? out_7 : 8'bz;  // Controlled_Buffer controlled_buffer_10
  assign out_8[7:0] = DATA_TO_ADDR_LO ? out_7 : 8'bz;  // Controlled_Buffer controlled_buffer_11
  assign out_8[15:8] = DATA_TO_ADDR_HI ? out_7 : 8'bz;  // Controlled_Buffer controlled_buffer_12
  Demultiplexer #(.select(3)) demultiplexer_3 (
    .out1(ADDR_TO_IP), .out2(ADDR_TO_HL), .out3(ADDR_TO_T), .out4(ADDR_TO_SP), .out5(MAR_INC),
    .out6(ADDR_TO_MAR), .out7(DATA_TO_IR), .in(1'b1), .sel({rom_3_data[2], rom_2_data_3}), .en(1'b1));  // open: out0
  ROM #(.addrWidth(15)) rom_3 (
    .addr({1'b0, _C_Z[1:0], out_6, out_10}),
    .data({T_RST, CARRY, L_TO_DATA, H_TO_DATA, rom_3_data_2, rom_3_data[2]}), .sel(1'b1));
  or or_3 (or_3_out, ADDR_TO_SP, SP_DEC);
  or or_4 (or_4_out, SP_DEC, SP_INC);
  Counter #(.width(16), .max('hffff)) counter_2 (
    .load(ADDR_TO_IP), .D(out_8), .count(IP_INC), .Q(out_9), .clk(CLK), .clr(RST));  // open: carry
  Counter #(.width(16), .max('hffff)) counter_3 (
    .load(ADDR_TO_MAR), .D(out_8), .count(MAR_INC), .Q(out_12), .clk(CLK));  // open: carry, clr
  Register #(.width(16)) register_8 (.D(out_8), .en(ADDR_TO_HL), .Q({out_17, L_Register}), .clk(CLK));  // open: clr
  Register #(.width(16)) register_9 (.D(out_8), .en(ADDR_TO_T), .Q(out_21), .clk(CLK), .clr(T_RST));
  Counter #(.width(16), .max('hffff)) counter_4 (
    .load(or_3_out), .D(out_8), .count(or_4_out), .Q(out_23), .clk(CLK), .clr(RST));  // open: carry
  Demultiplexer #(.select(3)) demultiplexer_4 (
    .out1(IP_TO_ADDR), .out2(HL_TO_ADDR), .out3(T_TO_ADDR), .out4(SP_TO_ADDR), .out5(IP_INC), .out6(SP_INC),
    .out7(SP_DEC), .in(1'b1), .sel(rom_3_data_2), .en(1'b1));  // open: out0
  and and_4 (and_4_out, ADDR_TO_IP, DATA_TO_ADDR_HI);
  and and_5 (and_5_out, ADDR_TO_IP, DATA_TO_ADDR_LO);
  RAM #(.addrWidth(16)) ram_1 (.addr(out_12), .data(out_15), .sel(1'b1), .clk(CLK), .ld(not_5_out));  // open: clr
  and and_6 (and_6_out, ADDR_TO_HL, DATA_TO_ADDR_HI);
  and and_7 (and_7_out, ADDR_TO_HL, DATA_TO_ADDR_LO);
  and and_8 (and_8_out, ADDR_TO_T, DATA_TO_ADDR_HI);
  and and_9 (and_9_out, ADDR_TO_T, DATA_TO_ADDR_LO);
  and and_10 (and_10_out, ADDR_TO_SP, DATA_TO_ADDR_HI);
  and and_11 (and_11_out, ADDR_TO_SP, DATA_TO_ADDR_LO);
  assign out_8[7:0] = or_5_out ? out_9[7:0] : 8'bz;  // Controlled_Buffer controlled_buffer_13
  assign out_8[15:8] = or_6_out ? out_9[15:8] : 8'bz;  // Controlled_Buffer controlled_buffer_14
  or or_5 (or_5_out, and_4_out, IP_TO_ADDR);
  or or_6 (or_6_out, IP_TO_ADDR, and_5_out);
  assign out_8[7:0] = or_7_out ? L_Register : 8'bz;  // Controlled_Buffer controlled_buffer_15
  assign out_8[15:8] = or_8_out ? out_17 : 8'bz;  // Controlled_Buffer controlled_buffer_16
  or or_7 (or_7_out, and_6_out, HL_TO_ADDR);
  or or_8 (or_8_out, HL_TO_ADDR, and_7_out);
  assign out_8[7:0] = or_9_out ? out_21[7:0] : 8'bz;  // Controlled_Buffer controlled_buffer_17
  assign out_8[15:8] = or_10_out ? out_21[15:8] : 8'bz;  // Controlled_Buffer controlled_buffer_18
  or or_9 (or_9_out, and_8_out, T_TO_ADDR);
  or or_10 (or_10_out, T_TO_ADDR, and_9_out);
  assign out_8[7:0] = or_11_out ? out_23[7:0] : 8'bz;  // Controlled_Buffer controlled_buffer_19
  assign out_8[15:8] = or_12_out ? out_23[15:8] : 8'bz;  // Controlled_Buffer controlled_buffer_20
  or or_11 (or_11_out, and_10_out, SP_TO_ADDR);
  or or_12 (or_12_out, SP_TO_ADDR, and_11_out);
  assign out_7 = ADDR_LO_TO_DATA ? out_8[7:0] : 8'bz;  // Controlled_Buffer controlled_buffer_21
  assign out_7 = ADDR_HI_TO_DATA ? out_8[15:8] : 8'bz;  // Controlled_Buffer controlled_buffer_22
  assign out_8 = in_5 ? in_3 : 16'bz;  // Controlled_Buffer controlled_buffer_23

  assign _C_Z[7:2] = {6{1'b0}};
  assign out_18 = {out_17, L_Register};

  // Other names for the same wires on the sheet: ZF = _C_Z[0]; CF = _C_Z[1]

  // Notes on the sheet:
  //   Microsequencer
  //   Control Unit
  //   Clock
  //   A Register
  //   X Register
  //   Adder / Subtractor
  //   Y Register
  //   B Register
  //   C Register
  //   D Register
  //   Instruction Register
  //   0-7
  //   contents of rom_1 (hex, n*v repeats v):
  //   512*0 4 14*0 4 5*0 4 58*0 6*18 0 0 6*18 0 0 12*18 4*0 18 0 18 0 18 0 18 0 18 4 18 20*0 4 53*0 4 11*0
  //   4 44*0 2 1 0 0 4 0 4 11*0 4 0 0 0 4 11*0 4 0 4 45*0 6*80 18 18 6*a0 18 18 80 a0 80 a0 80 a0 80 a0 80
  //   a0 80 a0 4*18 a0 0 a0 0 a0 4 a0 0 a0 0 a0 0 18 4 18 0 0 0 4 0 4 0 4 0 4 0 4 5*0 4 0 0 0 4 0 4 0 4 0
  //   4 5*0 4 0 4 0 0 0 4 0 4 0 4 4*0 4 4 0 4 0 4 0 0 0 4 0 4 5*0 4 0 4 0 4 0 4 0 0 0 4 5*0 4 0 4 0 4 0 4
  //   0 4 6*0 10 112*0 6*40 80 80 6*40 a0 a0 12*40 80 a0 80 a0 40 0 40 0 40 0 40 0 40 0 40 4 a0 0 a0 0 0 4
  //   10*0 4 0 4 4*0 4 8*0 4 0 4 4 5*0 4 6*0 4 0 4 8*0 4 4*0 4 0 4 8*0 4 0 4 0 0 4 0 4 4*0 4 7*0 4 4 0 4 8
  //   4 0 4 0 4 0 4 0 4 0 4 101*0 6*4 40 40 6*4 40 40 12*4 4*40 4 0 4 0 4 0 4 0 4 0 4 0 40 0 40 0 4 17*0 4
  //   17*0 4 17*0 4 17*0 4 17*0 4 4*0 80 37*0 4 8*0 4 0 0 4 12*0 4 4 14*0 4 39*0 4 4 6*0 4 4 12*0 4*4 7*0
  //   4 4*0 4 0 4 4 63*0 4 31*0 18 255*0 80 173*0 4 15*0 4 15*0 4 15*0 4 0 0 0 4 9*0 4 0 4 7*0 4 7*0 4 0 0
  //   0 4 0 4 0 4 0 4 0 4 0 4 727*0 4 11*0 4 7*0 4 263*0 4 1312*0 4 14*0 4 15*0 4 48*0 6*18 0 0 6*18 0 0
  //   12*18 4*0 18 0 18 0 18 0 18 0 18 4 18 52*0 4 21*0 4 15*0 4 40*0 2 1 0 0 4 0 4 11*0 4 0 0 0 4 11*0 4
  //   0 4 45*0 6*80 18 18 6*a0 18 18 80 a0 80 a0 80 a0 80 a0 80 a0 80 a0 4*18 a0 0 a0 0 a0 4 a0 0 a0 0 a0
  //   0 18 4 18 0 0 0 4 0 4 0 4 0 4 0 4 4*0 4 4 0 0 0 4 0 4 0 4 0 4 5*0 4 0 4 0 0 0 4 0 4 0 4 5*0 4 0 4 0
  //   4 0 0 0 4 0 4 5*0 4 0 4 0 4 0 4 0 0 0 4 5*0 4 0 4 0 4 0 4 0 4 6*0 10 112*0 6*40 80 80 6*40 a0 a0
  //   12*40 80 a0 80 a0 40 0 40 0 40 0 40 0 40 0 40 4 a0 0 a0 0 0 4 10*0 4 0 4 4*0 4 8*0 4 0 4 6*0 4 6*0 4
  //   0 4 8*0 4 4*0 4 0 4 4 7*0 4 0 4 0 0 4 0 4 8*0 4 0 0 0 4 4 0 4 8 4 0 4 0 4 0 4 0 4 0 4 101*0 6*4 40
  //   40 6*4 40 40 12*4 4*40 4 0 4 0 4 0 4 0 4 0 4 0 40 0 40 0 4 17*0 4 17*0 4 17*0 4 17*0 4 17*0 4 4*0 80
  //   37*0 4 8*0 4 0 0 4 0 0 0 4 8*0 4 15*0 4 39*0 4 4 6*0 4 4 12*0 4*4 7*0 4 4*0 4 0 4 4 31*0 4 63*0 18
  //   255*0 80 173*0 4 15*0 4 15*0 4 15*0 4 0 0 0 4 9*0 4 0 4 0 0 0 4 11*0 4 0 0 0 4 0 4 0 4 0 4 0 4 0 4
  //   727*0 4 11*0 4 0 0 0 4 267*0 4 1312*0 4 16*0 4 0 0 0 4 58*0 6*18 0 0 6*18 0 0 12*18 4*0 18 0 18 0 18
  //   0 18 0 18 0 18 0 0 4 17*0 4 59*0 4 5*0 4 44*0 2 1 0 0 4 0 4 11*0 4 0 0 0 4 11*0 4 0 4 45*0 6*80 18
  //   18 6*a0 18 18 80 a0 80 a0 80 a0 80 a0 80 a0 80 a0 4*18 a0 0 a0 0 a0 4 a0 0 a0 4 a0 0 18 0 18 0 0 0 4
  //   0 4 0 4 0 4 0 4 5*0 4 0 0 0 4 0 4 0 4 0 4 5*0 4 0 4 0 0 0 4 0 4 0 4 4*0 4 4 0 4 0 4 0 0 0 4 0 4 5*0
  //   4 0 4 0 4 0 4 0 0 0 4 5*0 4 0 4 0 4 0 4 0 4 6*0 10 112*0 6*40 80 80 6*40 a0 a0 12*40 80 a0 80 a0 40
  //   0 40 0 40 0 40 0 40 0 40 0 a0 0 a0 4 0 4 10*0 4 0 4 4*0 4 8*0 4 0 4 4 5*0 4 6*0 4 0 4 8*0 4 4*0 4 0
  //   4 10*0 4 0 0 4 0 4 4 0 0 0 4 7*0 4 4 0 4 8 4 0 4 0 4 0 4 0 4 0 4 101*0 6*4 40 40 6*4 40 40 12*4 4*40
  //   4 0 4 0 4 0 4 0 4 0 4 0 40 0 40 0 4 17*0 4 17*0 4 17*0 4 17*0 4 17*0 4 4*0 80 37*0 4 8*0 4 4 14*0 4
  //   4 14*0 4 39*0 4 4 6*0 4 4 12*0 4*4 7*0 4 0 0 0 4 4 0 4 64*0 4 31*0 18 255*0 80 173*0 4 15*0 4 15*0 4
  //   15*0 4 0 0 0 4 0 0 0 4 7*0 4 7*0 4 7*0 4 0 0 0 4 0 4 0 4 0 4 0 4 0 4 727*0 4 0 0 0 4 15*0 4 263*0 4
  //   1312*0 4 16*0 4 13*0 4 48*0 6*18 0 0 6*18 0 0 12*18 4*0 18 0 18 0 18 0 18 0 18 0 18 0 0 4 49*0 4
  //   27*0 4 9*0 4 40*0 2 1 0 0 4 0 4 11*0 4 0 0 0 4 11*0 4 0 4 45*0 6*80 18 18 6*a0 18 18 80 a0 80 a0 80
  //   a0 80 a0 80 a0 80 a0 4*18 a0 0 a0 0 a0 4 a0 0 a0 4 a0 0 18 0 18 0 0 0 4 0 4 0 4 0 4 0 4 4*0 4 4 0 0
  //   0 4 0 4 0 4 0 4 5*0 4 0 4 0 0 0 4 0 4 0 4 5*0 4 0 4 0 4 0 0 0 4 0 4 5*0 4 0 4 0 4 0 4 0 0 0 4 5*0 4
  //   0 4 0 4 0 4 0 4 6*0 10 112*0 6*40 80 80 6*40 a0 a0 12*40 80 a0 80 a0 40 0 40 0 40 0 40 0 40 0 40 0
  //   a0 0 a0 4 0 4 10*0 4 0 4 4*0 4 8*0 4 0 4 6*0 4 6*0 4 0 4 8*0 4 4*0 4 0 4 4 9*0 4 0 0 4 0 4 4 7*0 4 0
  //   0 0 4 4 0 4 8 4 0 4 0 4 0 4 0 4 0 4 101*0 6*4 40 40 6*4 40 40 12*4 4*40 4 0 4 0 4 0 4 0 4 0 4 0 40 0
  //   40 0 4 17*0 4 17*0 4 17*0 4 17*0 4 17*0 4 4*0 80 37*0 4 8*0 4 4 5*0 4 8*0 4 15*0 4 39*0 4 4 6*0 4 4
  //   12*0 4*4 7*0 4 0 0 0 4 4 0 4 32*0 4 63*0 18 255*0 80 173*0 4 15*0 4 15*0 4 15*0 4 0 0 0 4 0 0 0 4
  //   7*0 4 0 0 0 4 11*0 4 0 0 0 4 0 4 0 4 0 4 0 4 0 4 727*0 4 0 0 0 4 11*0 4 267*0 4
  //   Flags
  //   8-15
  //   contents of rom_2 (hex, n*v repeats v):
  //   256*80 256*e8 0 0 80 0 80 80 8*0 40 0 40 80 0 0 40 9*0 40 80 14*0 40 33*0 6*8 80 40 6*8 80 40 8 8 10
  //   10 18 18 20 20 4*0 80 80 40 40 8 0 10 0 18 40 20 40 4*0 80 40 40 40 0 80 11 0 19 0 21 0 1 0 1 0 80
  //   40 40 0 a 0 0 80 1a 0 22 0 2 0 2 0 80 40 40 0 b 0 13 0 0 80 23 0 3 0 3 0 80 40 40 40 c 0 14 0 1c 0 0
  //   80 4 0 4 0 80 40 40 40 8e 0 96 40 9e 0 a6 0 0 80 86 0 80 40 40 40 8f 0 97 0 9f 0 a7 40 87 0 0 80 80
  //   40 40 40 80 40 80 40 80 40 80 40 80 40 80 40 25*0 6f 8*0 af 0 0 6f 12*0 6f 6f 14*0 2f 33*0 6*1 28 28
  //   6*1 28 28 12*1 4*28 7*0 6f 4*0 28 0 28 6f 80 29 10*0 29 ef 29 0 0 0 80 2a 8*0 2a ef 2a 5*0 80 2b 6*0
  //   2b ef 2b 7*0 80 2c 4*0 2c ef 2c 6f 0 80 0 ef 4*0 80 ae 0 80 ae ef ae ef 5*0 80 0 ef 0 0 80 af af ef
  //   af 29 d ef 15 ef 1d ef 25 ef 5 ef 5 ef 25*0 80 8*0 40 0 0 80 12*0 40 80 14*0 40 39*0 1 1 6*0 1 1
  //   12*0 4*1 7*0 40 7*0 40 d 12*0 40 4*0 15 10*0 40 6*0 1d 8*0 40 8*0 25 6*0 40 0 40 0 35 0 40 4*0 5 0 0
  //   35 0 40 0 40 5*0 35 0 40 0 0 5 0 0 40 0 0 0 40 0 40 0 40 0 40 0 40 0 40 25*0 6e 8*0 ae 0 0 6e 12*0
  //   6e 6e 14*0 2e 72*0 6e 7*0 6e 13*0 ee 15*0 ee 15*0 ee 15*0 ee 0 6e 0 80 0 ee 7*0 80 0 ee 0 ee 5*0 80
  //   0 ee 5*0 ee 0 1 0 ee 0 ee 0 ee 0 ee 0 ee 0 ee 161*0 80 15*0 80 15*0 80 15*0 80 0 0 0 3d 0 80 7*0 3d
  //   0 80 0 80 5*0 3d 0 80 5*0 80 0 88 0 80 0 80 0 80 0 80 0 80 0 80 161*0 29 15*0 2a 15*0 2b 15*0 2c 0 0
  //   0 40 0 35 7*0 40 0 ae 0 35 5*0 40 0 35 5*0 af 0 c7 0 d 0 15 0 1d 0 25 0 5 0 5 215*0 80 11*0 80 7*0
  //   80 7*0 35 227*0 3d 11*0 3d 7*0 3d 7*0 80 227*0 40 11*0 40 7*0 40 7*0 3d 255*0 40 1056*0 256*80
  //   256*e8 0 0 80 0 80 80 8*0 40 0 40 80 0 0 40 80 8*0 40 15*0 40 33*0 6*8 80 40 6*8 80 40 8 8 10 10 18
  //   18 20 20 4*0 80 80 40 40 8 0 10 0 18 40 20 40 4*0 80 40 40 40 0 80 11 0 19 0 21 0 1 0 1 0 80 40 40
  //   40 a 0 0 80 1a 0 22 0 2 0 2 0 80 40 40 40 b 0 13 0 0 80 23 0 3 0 3 0 80 40 40 0 c 0 14 0 1c 0 0 80 4
  //   0 4 0 80 40 40 0 8e 0 96 40 9e 0 a6 0 0 80 86 0 80 40 40 40 8f 0 97 40 9f 0 a7 0 87 0 0 80 80 40 40
  //   40 80 40 80 40 80 40 80 40 80 40 80 40 25*0 6f 8*0 af 0 0 6f 0 0 0 6f 8*0 6f 15*0 2f 33*0 6*1 28 28
  //   6*1 28 28 12*1 4*28 7*0 6f 4*0 28 0 28 6f 80 29 10*0 29 ef 29 0 0 0 80 2a 8*0 2a ef 2a 6f 4*0 80 2b
  //   6*0 2b ef 2b 7*0 80 2c 4*0 2c ef 2c 0 0 80 0 ef 4*0 80 ae 0 80 ae ef ae ef 0 80 0 ef 6*0 80 af af ef
  //   af 29 d ef 15 ef 1d ef 25 ef 5 ef 5 ef 25*0 80 8*0 40 0 0 80 0 0 0 80 8*0 40 15*0 40 39*0 1 1 6*0 1
  //   1 12*0 4*1 7*0 40 7*0 40 d 12*0 40 4*0 15 10*0 40 0 40 4*0 1d 8*0 40 8*0 25 6*0 40 0 0 0 35 0 40 4*0
  //   5 0 0 35 0 40 0 40 0 35 0 40 6*0 5 0 0 40 0 0 0 40 0 40 0 40 0 40 0 40 0 40 25*0 6e 8*0 ae 0 0 6e 0
  //   0 0 6e 8*0 6e 15*0 2e 72*0 6e 7*0 6e 13*0 ee 15*0 ee 0 6e 13*0 ee 15*0 ee 0 0 0 80 0 ee 7*0 80 0 ee
  //   0 ee 0 80 0 ee 9*0 ee 0 1 0 ee 0 ee 0 ee 0 ee 0 ee 0 ee 161*0 80 15*0 80 15*0 80 15*0 80 0 0 0 3d 0
  //   80 7*0 3d 0 80 0 80 0 3d 0 80 9*0 80 0 88 0 80 0 80 0 80 0 80 0 80 0 80 161*0 29 15*0 2a 15*0 2b
  //   15*0 2c 0 0 0 40 0 35 7*0 40 0 ae 0 35 0 40 0 35 9*0 af 0 c7 0 d 0 15 0 1d 0 25 0 5 0 5 215*0 80
  //   11*0 80 0 0 0 80 11*0 35 227*0 3d 11*0 3d 0 0 0 3d 11*0 80 227*0 40 11*0 40 0 0 0 40 11*0 3d 255*0
  //   40 1056*0 256*80 256*e8 0 0 80 0 80 80 8*0 40 80 40 0 0 0 40 9*0 40 80 14*0 40 33*0 6*8 80 40 6*8 80
  //   40 8 8 10 10 18 18 20 20 4*0 80 80 40 40 8 0 10 0 18 40 20 40 0 40 0 40 80 0 40 0 0 80 11 0 19 0 21
  //   0 1 0 1 0 80 40 40 0 a 0 0 80 1a 0 22 0 2 0 2 0 80 40 40 0 b 0 13 0 0 80 23 0 3 0 3 0 80 40 40 40 c
  //   0 14 0 1c 0 0 80 4 0 4 0 80 40 40 40 8e 0 96 40 9e 0 a6 40 0 80 86 0 80 40 40 0 8f 0 97 0 9f 0 a7 0
  //   87 0 0 80 80 40 40 40 80 40 80 40 80 40 80 40 80 40 80 40 25*0 6f 8*0 af 6f 14*0 6f 6f 14*0 2f 33*0
  //   6*1 28 28 6*1 28 28 12*1 4*28 7*0 6f 0 0 0 6f 28 0 28 0 80 29 10*0 29 ef 29 0 0 0 80 2a 8*0 2a ef 2a
  //   5*0 80 2b 6*0 2b ef 2b 7*0 80 2c 4*0 2c ef 2c 6f 0 80 0 ef 0 80 0 ef 80 ae 0 0 ae ef ae 6*0 80 0 ef
  //   0 0 80 af af ef af 29 d ef 15 ef 1d ef 25 ef 5 ef 5 ef 25*0 80 8*0 40 80 14*0 40 80 14*0 40 39*0 1 1
  //   6*0 1 1 12*0 4*1 7*0 40 0 0 0 40 4*0 d 12*0 40 4*0 15 10*0 40 6*0 1d 8*0 40 8*0 25 6*0 40 0 40 0 35
  //   0 40 0 35 0 40 5 4*0 40 7*0 35 0 40 0 0 5 0 0 40 0 0 0 40 0 40 0 40 0 40 0 40 0 40 25*0 6e 8*0 ae 6e
  //   14*0 6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
  //   8-Bit Data Bus
  //   Z Register
  //   16-23
  //   contents of rom_3 (hex, n*v repeats v):
  //   256*3 256*b 0 0 2 0 8 9 8*0 b 0 4 9 0 0 8 9*0 b 9 5 0 3 11*0 b 39*0 5 b 6*0 5 b 8*0 10 10 20 20 5 5
  //   b b 5*0 4 0 1 10 0 20 a 5 4 b 1 e 9 6*0 10 0 20 0 5 b b 0 0 0 e 9 4*0 10 0 20 0 5 b b a 4*0 e 9 0 0
  //   10 0 20 0 5 b b 4 6*0 e 9 10 0 20 0 5 b b 1 0 e 0 b 0 0 0 a e 9 20 e 5 b b b 0 0 0 a 0 e 0 b 10 0 e
  //   9 5 b b b 5 b 5 b 5 b 5 b 5 b 5 b 25*0 c 11*0 c 13*0 c 14*0 1 76*0 a 4*0 9 c 16*0 9 c 11*0 a 4*0 9 c
  //   16*0 9 c 9*0 9 5*0 a 9 c 0 9 7*0 a 0 9 4*0 9 c 12*0 10 0 20 26*0 9 8*0 b 0 0 9 12*0 b 9 14*0 b 72*0
  //   1 7*0 1 13*0 b 15*0 b 15*0 b 15*0 b 0 1 0 e 0 b 4*0 10 0 0 e 0 b 0 b 5*0 e 0 b 0 0 20 0 0 b 0 0 0 b
  //   0 b 0 b 0 b 0 b 0 b 25*0 c 11*0 c 13*0 c 14*0 1 146*0 9 0 e 7*0 9 0 0 0 e 5*0 9 0 e 7*0 e 173*0 7
  //   15*0 7 15*0 7 15*0 7 0 0 0 2 0 9 7*0 2 0 7 0 9 5*0 2 0 9 5*0 7 0 89 0 7 0 7 0 7 0 7 0 7 0 7 213*0 4
  //   0 e 7*0 4 0 0 0 e 5*0 4 0 e 17*0 10 0 20 215*0 9 11*0 9 7*0 9 7*0 e 227*0 2 11*0 2 7*0 2 7*0 9 227*0
  //   6 11*0 6 7*0 6 7*0 2 255*0 6 1056*0 256*3 256*b 0 0 2 0 8 9 8*0 b 0 4 9 0 0 8 9 8*0 b 0 5 0 3 11*0 b
  //   39*0 5 b 6*0 5 b 8*0 10 10 20 20 5 5 b b 5*0 4 0 1 10 0 20 a 5 4 b 1 e 9 6*0 10 0 20 0 5 b b 4 0 0 e
  //   9 4*0 10 0 20 0 5 b b 1 4*0 e 9 0 0 10 0 20 0 5 b b 7*0 e 9 10 0 20 0 5 b b a 0 e 0 b 0 0 0 a e 9 20
  //   e 5 b b b 0 e 0 b 0 0 0 a 10 0 e 9 5 b b b 5 b 5 b 5 b 5 b 5 b 5 b 25*0 c 11*0 c 0 0 0 c 24*0 1 76*0
  //   a 4*0 9 c 16*0 9 c 16*0 9 c 16*0 9 c 7*0 a 0 9 5*0 a 9 c 0 9 5*0 9 5*0 a 0 0 9 c 12*0 10 0 20 26*0 9
  //   8*0 b 0 0 9 0 0 0 9 8*0 b 15*0 b 72*0 1 7*0 1 13*0 b 15*0 b 0 1 13*0 b 15*0 b 0 0 0 e 0 b 4*0 10 0 0
  //   e 0 b 0 b 0 e 0 b 6*0 20 0 0 b 0 0 0 b 0 b 0 b 0 b 0 b 0 b 25*0 c 11*0 c 0 0 0 c 24*0 1 146*0 9 0 e
  //   7*0 9 0 0 0 e 0 9 0 e 11*0 e 173*0 7 15*0 7 15*0 7 15*0 7 0 0 0 2 0 9 7*0 2 0 7 0 9 0 2 0 9 9*0 7 0
  //   89 0 7 0 7 0 7 0 7 0 7 0 7 213*0 4 0 e 7*0 4 0 0 0 e 0 4 0 e 21*0 10 0 20 215*0 9 11*0 9 0 0 0 9
  //   11*0 e 227*0 2 11*0 2 0 0 0 2 11*0 9 227*0 6 11*0 6 0 0 0 6 11*0 2 255*0 6 1056*0 256*3 256*b 0 0 2
  //   0 8 9 8*0 b 9 4 0 0 0 8 9*0 b 9 5 0 3 11*0 b 39*0 5 b 6*0 5 b 8*0 10 10 20 20 5 5 b b 5*0 4 0 1 10 4
  //   20 1 5 0 b a e 9 6*0 10 0 20 0 5 b b 0 0 0 e 9 4*0 10 0 20 0 5 b b a 4*0 e 9 0 0 10 0 20 0 5 b b 4
  //   6*0 e 9 10 0 20 0 5 b b 1 0 e 0 b 0 e 0 b e 9 20 0 5 b b a 0 0 0 a 0 e 0 0 10 0 e 9 5 b b b 5 b 5 b
  //   5 b 5 b 5 b 5 b 25*0 c 9*0 c 15*0 c 14*0 1 33*0 6*40 0 0 6*40 33*0 a 9 c 16*0 9 c 11*0 a 4*0 9 c
  //   16*0 9 c 9*0 9 0 0 0 9 0 0 9 c 5*0 a 0 0 0 a 0 9 4*0 9 c 12*0 10 0 20 26*0 9 8*0 b 9 14*0 b 9 14*0 b
  //   39*0 40 40 6*0 40 40 23*0 1 0 0 0 1 17*0 b 15*0 b 15*0 b 15*0 b 0 1 0 e 0 b 0 e 0 b 10 4*0 b 7*0 e 0
  //   b 0 0 20 0 0 b 0 0 0 b 0 b 0 b 0 b 0 b 0 b 25*0 c 9*0 c 15*0 c 14*0 1 146*0 9 0 e 0 9 0 e 13*0 9 0 e
  //   7*0 e 173*0 7 15*0 7 15*0 7 15*0 7 0 0 0 2 0 9 0 2 0 9 5*0 7 7*0 2 0 9 5*0 7 0 89 0 7 0 7 0 7 0 7 0
  //   7 0 7 213*0 4 0 e 0 4 0 e 13*0 4 0 e 17*0 10 0 20 215*0 9 0 0 0 9 15*0 9 7*0 e 227*0 2 0 0 0 2 15*0
  //   2 7*0 9 227*0 6 0 0 0 6 15*0 6 7*0 2 255*0 6 1056*0 256*3 256*b 0 0 2 0 8 9 8*0 b 9 4 0 0 0 8 9 8*0
  //   b 0 5 0 3 11*0 b 39*0 5 b 6*0 5 b 8*0 10 10 20 20 5 5 b b 5*0 4 0 1 10 4 20 1 5 0 b a e 9 6*0 10 0
  //   20 0 5 b b 4 0 0 e 9 4*0 10 0 20 0 5 b b 1 4*0 e 9 0 0 10 0 20 0 5 b b 7*0 e 9 10 0 20 0 5 b b a 0 e
  //   0 b 0 e 0 b e 9 20 0 5 b b a 0 e 5*0 a 10 0 e 9 5 b b b 5 b 5 b 5 b 5 b 5 b 5 b 25*0 c 9*0 c 5*0 c
  //   24*0 1 33*0 6*40 0 0 6*40 33*0 a 9 c 16*0 9 c 16*0 9 c 16*0 9 c 7*0 a 0 9 0 0 0 9 0 0 9 c 5*0 a 0 9
  //   5*0 a 0 0 9 c 12*0 10 0 20 26*0 9 8*0 b 9 5*0 9 8*0 b 15*0 b 39*0 40 40 6*0 40 40 23*0 1 0 0 0 1
  //   17*0 b 15*0 b 0 1 13*0 b 15*0 b 0 0 0 e 0 b 0 e 0 b 10 4*0 b 0 0 0 e 0 b 6*0 20 0 0 b 0 0 0 b 0 b 0
  //   b 0 b 0 b 0 b 25*0 c 9*0 c 5*0 c 24*0 1 146*0 9 0 e 0 9 0 e 9*0 9 0 e 11*0 e 173*0 7 15*0 7 15*0 7
  //   15*0 7 0 0 0 2 0 9 0 2 0 9 5*0 7 0 0 0 2 0 9 9*0 7 0 89 0 7 0 7 0 7 0 7 0 7 0 7 213*0 4 0 e 0 4 0 e
  //   9*0 4 0 e 21*0 10 0 20 215*0 9 0 0 0 9 11*0 9 11*0 e 227*0 2 0 0 0 2 11*0 2 11*0 9 227*0 6 0 0 0 6
  //   11*0 6 11*0 2 255*0 6
  //   Memory Address Register
  //   H Register
  //   Instruction Pointer
  //   Memory Data Register
  //   HL Register
  //   T Register
  //   Stack Pointer
  //   16-Bit Address Bus
endmodule
