// Logisim project 2x4-add-sub.circ as structural Verilog: 1 circuit, main circuit main
module main (
  input  [7:0] X,
  input  Z_TO_DATA,
  input  FLAGS,
  input  CARRY,
  input  SUB,
  input  [7:0] Y,
  output [7:0] Z,
  output [7:0] DATA,
  output ZF,
  output CF,
  output [7:0] _C_Z
);

  wire adder_1_cout, adder_2_cout, CLK, d_ff_1_q, d_ff_2_q, nor_1_out, RST, xor_1_out, xor_3_out;
  wire [3:0] bit_extender_1_out, xor_2_out, xor_4_out;

  Button u_CLK (.out(CLK));
  Button u_RST (.out(RST));
  assign bit_extender_1_out = {{3{SUB}}, SUB};  // Bit_Extender bit_extender_1
  xor xor_1 (xor_1_out, CARRY, SUB);
  assign xor_2_out = bit_extender_1_out ^ Y[7:4];  // XOR_Gate xor_2, 4 bits wide
  Adder #(.width(4)) adder_1 (.a(X[7:4]), .b(xor_2_out), .out(Z[7:4]), .cin(adder_2_cout), .cout(adder_1_cout));
  xor xor_3 (xor_3_out, adder_1_cout, SUB);
  assign xor_4_out = bit_extender_1_out ^ Y[3:0];  // XOR_Gate xor_4, 4 bits wide
  Adder #(.width(4)) adder_2 (.a(X[3:0]), .b(xor_4_out), .out(Z[3:0]), .cin(xor_1_out), .cout(adder_2_cout));
  nor nor_1 (nor_1_out, Z[0], Z[1], Z[2], Z[3], Z[4], Z[5], Z[6], Z[7]);
  assign DATA = Z_TO_DATA ? Z : 8'bz;  // Controlled_Buffer controlled_buffer_1
  D_Flip_Flop d_ff_1 (.clk(CLK), .D(nor_1_out), .Q(d_ff_1_q), .en(Z_TO_DATA));  // open: Qn, preset, reset
  D_Flip_Flop d_ff_2 (.clk(CLK), .D(xor_3_out), .Q(d_ff_2_q), .en(Z_TO_DATA));  // open: Qn, preset, reset
  D_Flip_Flop d_ff_3 (.clk(CLK), .D(d_ff_1_q), .Q(_C_Z[0]), .en(FLAGS), .reset(RST));  // open: Qn, preset
  D_Flip_Flop d_ff_4 (.clk(CLK), .D(d_ff_2_q), .Q(_C_Z[1]), .en(FLAGS), .reset(RST));  // open: Qn, preset

  assign _C_Z[7:2] = {6{1'b0}};
  assign CF = _C_Z[1];
  assign ZF = _C_Z[0];
endmodule
