// Logisim project add-sub.circ as structural Verilog: 1 circuit, main circuit main
module main (
  input  CARRY,
  input  [7:0] A,
  input  [7:0] B,
  input  SUB,
  input  [3:0] in_5,
  input  [3:0] in_6,
  input  in_7,
  input  [3:0] in_8,
  input  [3:0] in_9,
  output [7:0] out_10,
  output [3:0] out_11,
  output [3:0] out_12
);

  wire adder_3_cout, xor_1_out;
  wire [3:0] bit_extender_2_out, xor_3_out, xor_4_out;
  wire [7:0] bit_extender_1_out, xor_2_out;

  assign bit_extender_1_out = {{7{SUB}}, SUB};  // Bit_Extender bit_extender_1
  xor xor_1 (xor_1_out, CARRY, SUB);
  assign xor_2_out = B ^ bit_extender_1_out;  // XOR_Gate xor_2, 8 bits wide
  assign bit_extender_2_out = {{3{in_7}}, in_7};  // Bit_Extender bit_extender_2
  Adder adder_1 (.a(A), .b(xor_2_out), .out(out_10), .cin(xor_1_out));  // open: cout
  assign xor_3_out = bit_extender_2_out ^ in_8;  // XOR_Gate xor_3, 4 bits wide
  Adder #(.width(4)) adder_2 (.a(in_5), .b(xor_3_out), .out(out_11), .cin(adder_3_cout));  // open: cout
  assign xor_4_out = bit_extender_2_out ^ in_9;  // XOR_Gate xor_4, 4 bits wide
  Adder #(.width(4)) adder_3 (.a(in_6), .b(xor_4_out), .out(out_12), .cin(in_7), .cout(adder_3_cout));
endmodule
