// Logisim project ram-rom.circ as structural Verilog: 1 circuit, main circuit main
module main (
);

  RAM #(.addrWidth(15)) ram_1 ();  // open: addr, data, sel, clk, ld, clr
  ROM #(.addrWidth(11)) rom_1 ();  // open: addr, data, sel
  RAM #(.addrWidth(17)) ram_2 ();  // open: addr, data, sel, clk, ld, clr
  ROM #(.addrWidth(13)) rom_2 ();  // open: addr, data, sel
  RAM #(.addrWidth(19)) ram_3 ();  // open: addr, data, sel, clk, ld, clr
  ROM #(.addrWidth(15)) rom_3 ();  // open: addr, data, sel

  // Notes on the sheet:
  //   AS6C62256 (32K)
  //   AT28C16A (2K)
  //   AS6C1008 (128K)
  //   AT28C64B (8K)
  //   AS6C4008 (512K)
  //   AT28C256 (32K)
endmodule
